# Fritzing sketch Sketch (saved by Fritzing 0.9.3b)
breadboards: 1

parts:
  Arduino_UNO = Arduino Uno (Rev3) - ICSP
  Resistor_220_Ohm = Resistor [tolerance=±5% resistance=10k package="2512 [SMD]"]
  Potentiometer = Rotary Potentiometer (Small) [maximum_resistance=100kΩ package=THT]
  Analog_Digital_Converter = ADS1115 16-bit ADC Breakout
  BME280 = BME280
  M1 = ph-4502c [package=THT]
  Capacitive_Soil_Moisture_Sensor = Capacitive Soil Moisture Sensor V2.0
  S1 = LDR light sensor [package=THT]
  Espessif_Serial_Wifi_Modul_1 = ESP8266 ESP01 [part_number=ESP8266 package=THT]
  Capacitor_0_1uF = Capacitor [package=cap-pth-small2]
  Capacitor_100uF = Electrolytic Capacitor [capacitance=100µF package="100 mil [THT, electrolytic]"]
  U1 = AMS1117 step down module
  GLCD_128x64 = 128 x 64 Graphic LCD
  R1 = Resistor [tolerance=±5% resistance=10k package="1206 [SMD]"]
  R3 = Resistor [tolerance=±5% resistance=1k package="1206 [SMD]"]
  R4 = Resistor [tolerance=±5% resistance=2.2k package="1206 [SMD]"]
  R5 = Resistor [tolerance=±5% resistance=10k package="1206 [SMD]"]
  R2 = Resistor [tolerance=±5% resistance=10k package="1206 [SMD]"]
  Button_1 = Momentary Switch [package=ksa_sealed_tac_switch]
  Button_2 = Momentary Switch [package=ksa_sealed_tac_switch]
  Button_3 = Momentary Switch [package=ksa_sealed_tac_switch]
  Button_4 = Momentary Switch [package=ksa_sealed_tac_switch]

nets:
  N1: Arduino_UNO.A4/SDA, Analog_Digital_Converter.SDA, BME280.SDA
  N2: Arduino_UNO.A5/SCL, Analog_Digital_Converter.SCL, BME280.SCL
  N3: Arduino_UNO.D8, GLCD_128x64.7_DB0
  N4: Arduino_UNO.D9_PWM, GLCD_128x64.6_Enable
  N5: Arduino_UNO.D10_PWM/SS, GLCD_128x64.4_D/I
  N6: Arduino_UNO.D2, Espessif_Serial_Wifi_Modul_1.TXD
  N7: Arduino_UNO.D3_PWM, R3.Pin_0
  N8: Arduino_UNO.D4, Button_1.4
  N9: Arduino_UNO.D5_PWM, Button_2.4
  N10: Arduino_UNO.D6_PWM, Button_3.4
  N11: Arduino_UNO.D7, Button_4.4
  5V: Arduino_UNO.5V, Resistor_220_Ohm.Pin_0, Potentiometer.leg1, Analog_Digital_Converter.VDD, BME280.VIN, M1.pin6, Capacitive_Soil_Moisture_Sensor.VCC, S1.pin3, U1.VIN+, GLCD_128x64.2_Vdd, Button_1.3, Button_2.3, Button_3.3, Button_4.3
  GND: Arduino_UNO.GND, Potentiometer.leg2, Analog_Digital_Converter.GND, BME280.GND, M1.pin4, M1.pin5, Capacitive_Soil_Moisture_Sensor.GND, S1.pin2, Capacitor_100uF.-, U1.GND-, GLCD_128x64.1_Vss, GLCD_128x64.5_R/W, GLCD_128x64.20_K(-), R4.Pin_1
  N12: Resistor_220_Ohm.Pin_1, GLCD_128x64.19_A(+)
  N13: Potentiometer.wiper, GLCD_128x64.3_Vo
  N14: Analog_Digital_Converter.A0, M1.pin3
  N15: Analog_Digital_Converter.A1, M1.pin1
  N16: Analog_Digital_Converter.A2, Capacitive_Soil_Moisture_Sensor.AOUT
  N17: Analog_Digital_Converter.A3, S1.pin1
  N18: Espessif_Serial_Wifi_Modul_1.GND, Capacitor_0_1uF.1, Capacitor_100uF.+
  N19: Espessif_Serial_Wifi_Modul_1.RXD, R3.Pin_1, R4.Pin_0
  N20: Espessif_Serial_Wifi_Modul_1.VCC, Capacitor_0_1uF.2, U1.VOUT+, R1.Pin_0, R5.Pin_0, R2.Pin_0
  N21: Espessif_Serial_Wifi_Modul_1.GPIO00, R2.Pin_1
  N22: Espessif_Serial_Wifi_Modul_1.GPIO02, R1.Pin_1
  N23: Espessif_Serial_Wifi_Modul_1.CH_PD, R5.Pin_1

custom parts:
  ADS1115 16-bit ADC Breakout: ADS1015 12-bit I2C ADC+PGA Breakout
  ph-4502c: ph-4502c PH Meter.
  LDR light sensor: Light sensor module. 3.3 V to 5V power.
  ESP8266 ESP01: Generic WiFi Module based on the ESP8266 with onboard PCB antenna and UART communications
