# Fritzing sketch Sketch (saved by Fritzing 0.9.3b)
breadboards: 2

parts:
  Arduino_UNO = Arduino Uno (Rev3) - ICSP
  Voltage_Regulator = V_REG_LD1117VXX [package=78xxl]  # not connected
  GLCD_128x64 = 128 x 64 Graphic LCD
  Resistor_220_Ohm = Resistor [tolerance=±5% resistance=220 package="2512 [SMD]"]
  Potentiometer = Rotary Potentiometer (Small) [maximum_resistance=100kΩ package=THT]
  Button_4 = Momentary Switch [package=tactile-pth]
  Button_3 = Momentary Switch [package=tactile-pth]
  Button_2 = Momentary Switch [package=tactile-pth]
  Button_1 = Momentary Switch [package=tactile-pth]
  Analog_Digital_Converter = ADS1115 16-bit ADC Breakout
  BME280 = BME280
  M1 = ph-4502c [package=THT]
  Capacitive_Soil_Moisture_Sensor = Capacitive Soil Moisture Sensor V2.0
  S1 = LDR light sensor [package=THT]
  Espessif_Serial_Wifi_Modul_1 = ESP8266 ESP01 [part_number=ESP8266 package=THT]  # not connected

nets:
  N1: Arduino_UNO.A4/SDA, Analog_Digital_Converter.SDA, BME280.SDA
  N2: Arduino_UNO.A5/SCL, Analog_Digital_Converter.SCL, BME280.SCL
  N3: Arduino_UNO.D8, GLCD_128x64.7_DB0
  N4: Arduino_UNO.D9_PWM, GLCD_128x64.6_Enable
  N5: Arduino_UNO.D10_PWM/SS, GLCD_128x64.4_D/I
  N6: Arduino_UNO.D4, Button_1.2
  N7: Arduino_UNO.D5_PWM, Button_2.2
  N8: Arduino_UNO.D6_PWM, Button_3.2
  N9: Arduino_UNO.D7, Button_4.2
  5V: Arduino_UNO.5V, GLCD_128x64.2_Vdd, Resistor_220_Ohm.Pin_0, Potentiometer.leg1, Button_4.4, Button_3.4, Button_2.4, Button_1.4, Analog_Digital_Converter.VDD, BME280.VIN, M1.pin6, Capacitive_Soil_Moisture_Sensor.VCC, S1.pin3
  GND: Arduino_UNO.GND, GLCD_128x64.1_Vss, GLCD_128x64.5_R/W, GLCD_128x64.20_K(-), Potentiometer.leg2, Analog_Digital_Converter.GND, BME280.GND, M1.pin4, M1.pin5, Capacitive_Soil_Moisture_Sensor.GND, S1.pin2
  N10: GLCD_128x64.3_Vo, Potentiometer.wiper
  N11: GLCD_128x64.19_A(+), Resistor_220_Ohm.Pin_1
  N12: Analog_Digital_Converter.A0, M1.pin3
  N13: Analog_Digital_Converter.A1, M1.pin1
  N14: Analog_Digital_Converter.A2, Capacitive_Soil_Moisture_Sensor.AOUT
  N15: Analog_Digital_Converter.A3, S1.pin1

custom parts:
  ADS1115 16-bit ADC Breakout: ADS1015 12-bit I2C ADC+PGA Breakout
  ph-4502c: ph-4502c PH Meter.
  LDR light sensor: Light sensor module. 3.3 V to 5V power.
  ESP8266 ESP01: Generic WiFi Module based on the ESP8266 with onboard PCB antenna and UART communications
